# Fritzing sketch Shema (saved by Fritzing 0.9.3b)

parts:
  RAMPS_1_4 = RAMPS_1.4
  DRV8825 = Pololu A4988 [package=SO16]
  Pololu_A3 = Pololu A4988 [package=SO16]
  Pololu_A4 = Pololu A4988 [package=SO16]
  M5 = Stepper Motor - Bipolar
  M6 = Stepper Motor - Bipolar
  M7 = Stepper Motor - Bipolar
  RepRapDiscount_Smart_Controller = LCD screen
  U1 = microSD Socket [package="Molex 502774-0891 [SMD]"]  # not connected
  SW1 = ENCODER_RGB_CA [package=encoder_led_3]
  S1 = SWITCH-MOMENTARY-2 [package=tactile_switch_tall]
  J1 = Piezo Speaker

nets:
  N1: RAMPS_1_4.X-EN, DRV8825.ENABLE
  N2: RAMPS_1_4.X-MS1, DRV8825.MS1
  N3: RAMPS_1_4.X-MS2, DRV8825.MS2
  N4: RAMPS_1_4.X-MS3, DRV8825.MS3
  N5: RAMPS_1_4.X-RST, DRV8825.RESET
  N6: RAMPS_1_4.X-SLP, DRV8825.SLEEP
  N7: RAMPS_1_4.X-STEP, DRV8825.STEP
  N8: RAMPS_1_4.X-DIR, DRV8825.DIR
  N9: RAMPS_1_4.Y-EN, Pololu_A3.ENABLE
  N10: RAMPS_1_4.Y-MS1, Pololu_A3.MS1
  N11: RAMPS_1_4.Y-MS2, Pololu_A3.MS2
  N12: RAMPS_1_4.Y-MS3, Pololu_A3.MS3
  N13: RAMPS_1_4.Y-RST, Pololu_A3.RESET
  N14: RAMPS_1_4.Y-SLP, Pololu_A3.SLEEP
  N15: RAMPS_1_4.Y-STEP, Pololu_A3.STEP
  N16: RAMPS_1_4.Y-DIR, Pololu_A3.DIR
  N17: RAMPS_1_4.Z-EN, Pololu_A4.ENABLE
  N18: RAMPS_1_4.Z-MS1, Pololu_A4.MS1
  N19: RAMPS_1_4.Z-MS2, Pololu_A4.MS2
  N20: RAMPS_1_4.Z-MS3, Pololu_A4.MS3
  N21: RAMPS_1_4.Z-RST, Pololu_A4.RESET
  N22: RAMPS_1_4.Z-SLP, Pololu_A4.SLEEP
  N23: RAMPS_1_4.Z-STEP, Pololu_A4.STEP
  N24: RAMPS_1_4.Z-DIR, Pololu_A4.DIR
  N25: RAMPS_1_4.+12V, RAMPS_1_4.+D10, DRV8825.VMOT, Pololu_A3.VMOT, Pololu_A4.VMOT
  GND: RAMPS_1_4.GND, DRV8825.GND, Pololu_A3.GND, Pololu_A4.GND
  N26: RAMPS_1_4.X-2B, DRV8825.2B, M6.A
  N27: RAMPS_1_4.X-2A, DRV8825.2A, M6.C
  N28: RAMPS_1_4.X-1A, DRV8825.1A, M6.B
  N29: RAMPS_1_4.X-1B, DRV8825.1B, M6.D
  VDD: RAMPS_1_4.VCC, DRV8825.VDD, Pololu_A3.VDD, Pololu_A4.VDD
  N30: RAMPS_1_4.Y-2B, Pololu_A3.2B, M7.D
  N31: RAMPS_1_4.Y-2A, Pololu_A3.2A, M7.B
  N32: RAMPS_1_4.Y-1A, Pololu_A3.1A, M7.C
  N33: RAMPS_1_4.Y-1B, Pololu_A3.1B, M7.A
  N34: RAMPS_1_4.Z-2B, Pololu_A4.2B, M5.A
  N35: RAMPS_1_4.Z-2A, Pololu_A4.2A, M5.C
  N36: RAMPS_1_4.Z-1A#105, RAMPS_1_4.Z-1B#119, RAMPS_1_4.Z-1B#123, Pololu_A4.1A, M5.B
  N37: RAMPS_1_4.Z-1B#106, RAMPS_1_4.Z-1A#120, RAMPS_1_4.Z-1A#124, Pololu_A4.1B, M5.D
  N38: RAMPS_1_4.D32, RepRapDiscount_Smart_Controller.VSS
  N39: RAMPS_1_4.D47, RepRapDiscount_Smart_Controller.VDD
  N40: RAMPS_1_4.D45, RepRapDiscount_Smart_Controller.V0
  N41: RAMPS_1_4.D43, RepRapDiscount_Smart_Controller.RS
  N42: RAMPS_1_4.D41, RepRapDiscount_Smart_Controller.R/W
  N43: RAMPS_1_4.D39, RepRapDiscount_Smart_Controller.E
  N44: RAMPS_1_4.D37, RepRapDiscount_Smart_Controller.DB0
  N45: RAMPS_1_4.D35, RepRapDiscount_Smart_Controller.DB6, SW1.C
  N46: RAMPS_1_4.D33, J1.pin1
  N47: RAMPS_1_4.D31, J1.pin2
  N48: RAMPS_1_4.D29, S1.1
  N49: RAMPS_1_4.D27, S1.2

custom parts:
  RAMPS_1.4: Ramps 1.4 3d printer driver module. Pcb view has been supressed as not useful. Note you can drag the A4988 stepper controller over the sockets on the card and they will connect correctly (there is currently a Fritzing bug which will say there are connections unrouted however). At present the mega connections are not populated, although with work on schematic that could be done too.
